// Logisim project proj_2_1_top.circ as structural Verilog: 8 circuits, main circuit testbench
module TOP (
  input  clk,
  input  rst,
  input  [31:0] inst,
  output [31:0] inst_addr,
  output mem_wen,
  output [31:0] mem_din,
  output [31:0] mem_dout,
  output [31:0] mem_addr,
  output control_en,
  output [31:0] control_pc,
  output wb_en,
  output [4:0] wb_addr,
  output [31:0] wb_data
);

  wire alu_1_equal, B_type, beq_jump, if_beq, if_half, if_rs2, jal_or_jalr, pc_src, rs1_src;
  wire [1:0] wb_src;
  wire [2:0] ALU_control;
  wire [4:0] id_1_rs1, id_1_rs2;
  wire [31:0] adder_1_out, IMM, multiplexer_1_out, multiplexer_2_out, multiplexer_4_out, multiplexer_5_out,
       multiplexer_6_out, not_1_out, pc_before_align, PCPlus4, regfile_1_rs1_data;

  Multiplexer #(.width(32)) multiplexer_1 (.in0(PCPlus4), .in1(control_pc), .out(multiplexer_1_out), .sel(control_en));
  Adder #(.width(32)) adder_1 (.a(IMM), .b(inst_addr), .out(adder_1_out));  // open: cin, cout
  Register #(.width(32)) PC (.D(multiplexer_1_out), .clk(clk), .Q(inst_addr), .clr(rst));  // open: en
  or or_1 (control_en, jal_or_jalr, beq_jump);
  Multiplexer #(.width(32)) multiplexer_2 (.in0(adder_1_out), .in1(mem_addr), .out(multiplexer_2_out), .sel(pc_src));
  Adder #(.width(32)) adder_2 (.a(32'h4), .b(inst_addr), .out(PCPlus4));  // open: cin, cout
  Multiplexer #(.width(32)) multiplexer_3 (
    .in0({32{1'b0}}), .in1(multiplexer_2_out), .out(pc_before_align), .sel(B_type));
  Multiplexer #(.width(32)) multiplexer_4 (.in0(inst), .in1({32{1'b0}}), .out(multiplexer_4_out), .sel(rst));
  assign not_1_out = ~32'h1;  // NOT_Gate not_1, 32 bits wide
  assign control_pc = not_1_out & pc_before_align;  // AND_Gate and_1, 32 bits wide
  ID id_1 (.inst(multiplexer_4_out), .rd(wb_addr), .rs1(id_1_rs1), .rs2(id_1_rs2));
  Imm_gen imm_gen_1 (.inst(multiplexer_4_out), .imm(IMM));
  controller controller_1 (
    .inst(multiplexer_4_out), .is_beq(if_beq), .if_rs2(if_rs2), .we(mem_wen), .wb_src(wb_src), .wb_en(wb_en),
    .ALU_control(ALU_control), .pc_src(pc_src), .rs1_src(rs1_src), .jal_or_jalr(jal_or_jalr),
    .if_half(if_half), .B_type(B_type));
  and and_2 (beq_jump, alu_1_equal, if_beq);
  regfile regfile_1 (
    .reset(rst), .rs1(id_1_rs1), .rs2(id_1_rs2), .clk(clk), .wb_data(wb_data), .wb_en(wb_en),
    .wb_addr(wb_addr), .rs1_data(regfile_1_rs1_data), .rs2_data(mem_din));
  Multiplexer #(.width(32)) multiplexer_5 (
    .in0(inst_addr), .in1(regfile_1_rs1_data), .out(multiplexer_5_out), .sel(rs1_src));
  Multiplexer #(.width(32)) multiplexer_6 (.in0(mem_din), .in1(IMM), .out(multiplexer_6_out), .sel(if_rs2));
  ALU alu_1 (
    .rs1(multiplexer_5_out), .rs2_or_imm(multiplexer_6_out), .ALU_control(ALU_control), .result(mem_addr),
    .equal(alu_1_equal));
  mem mem_1 (
    .reset(rst), .mem_wen(mem_wen), .mem_din(mem_din), .mem_addr(mem_addr), .clk(clk), .if_half(if_half),
    .mem_dout(mem_dout));
  Multiplexer #(.select(2), .width(32)) multiplexer_7 (
    .in0(mem_dout), .in1(mem_addr), .in2(PCPlus4), .in3(IMM), .out(wb_data), .sel(wb_src));

  // Other names for the same wires on the sheet: ALU_result[31:0] = mem_addr; rd[4:0] = wb_addr; rs2[31:0] = mem_din

  // Notes on the sheet:
  //   DON'T TOUCH!
endmodule

module testbench (
  input  rst,
  output [5:0] out_2,
  output out_3,
  output halt,
  output [31:0] out_5,
  output [31:0] mem_dout,
  output [31:0] mem_addr,
  output out_8,
  output [31:0] out_9,
  output out_10,
  output [4:0] out_11,
  output [31:0] out_12
);

  wire and_1_out, carry, clk, not_1_out, not_2_out, por_1_out, rst_t;
  wire [31:0] inst, inst_addr;

  not not_1 (not_1_out, inst[2]);
  not not_2 (not_2_out, inst[3]);
  POR por_1 (.out(por_1_out));
  // Probe on inst_addr
  TOP top_1 (
    .clk(clk), .rst(rst_t), .inst(inst), .inst_addr(inst_addr), .mem_wen(out_3), .mem_din(out_5),
    .mem_dout(mem_dout), .mem_addr(mem_addr), .control_en(out_8), .control_pc(out_9), .wb_en(out_10),
    .wb_addr(out_11), .wb_data(out_12));
  Clock clock_1 (.out(clk));
  or or_1 (rst_t, rst, por_1_out);
  and and_1 (and_1_out, inst[0], inst[1], not_1_out, not_2_out, inst[4], inst[5], inst[6]);
  or or_2 (halt, and_1_out, carry);
  Counter #(.max('h3f), .width(6)) counter_1 (
    .clr(rst_t), .up(1'b1), .count(1'b1), .clk(clk), .carry(carry), .Q(out_2));  // open: load, D
  // ROM #(.line("quad"), .misaligned("true")) inst_mem: pin names not known; wires that end beside it: inst_addr[7:0], inst[7:0], inst[15:8], inst[23:16], inst[31:24]
  // Probe on inst

  // Other names for the same wires on the sheet: control_en = out_8; control_pc[31:0] = out_9; mem_din[31:0] = out_5;
  //   mem_wen = out_3; wb_addr[4:0] = out_11; wb_data[31:0] = out_12; wb_en = out_10

  // Notes on the sheet:
  //   DON'T TOUCH!
  //   contents of inst_mem (hex, n*v repeats v):
  //   37 1a 0 0 97 a 0 0 93 0 10 0 33 81 10 0 93 71 f1 f 13 d2 11 0 93 2 60 ff 33 d3 12 40 b3 a3 2 0 13 b4
  //   12 0 23 20 2a 0 23 12 3a 0 63 80 3 2 83 24 a 0 3 15 4a 0 ef 5 c0 0 63 8 c0 0 ef 9 40 1 13 6 50 1 67
  //   89 5 0 23 24 a 0 ef f8 df ff 23 24 1a 0 73 0 10 0 e3 8e 10 fe
  //   you can write any instruction in
endmodule

module mem (
  input  reset,
  input  mem_wen,
  input  [31:0] mem_din,
  input  [31:0] mem_addr,
  input  clk,
  input  if_half,
  output [31:0] mem_dout
);

  wire and_1_out, and_2_out, and_3_out, and_4_out, comparator_1_eq, comparator_2_eq, comparator_3_eq,
       comparator_4_eq, comparator_5_eq, comparator_6_eq, comparator_7_eq, comparator_8_eq, comparator_9_eq,
       comparator_10_eq, comparator_11_eq, comparator_12_eq, comparator_13_eq, comparator_14_eq,
       comparator_15_eq, comparator_16_eq, comparator_17_eq, comparator_18_eq, comparator_19_eq,
       comparator_20_eq, comparator_21_eq, comparator_22_eq, comparator_23_eq, comparator_24_eq,
       comparator_25_eq, comparator_26_eq, comparator_27_eq, comparator_28_eq, comparator_29_eq,
       comparator_30_eq, comparator_31_eq, comparator_32_eq, comparator_33_eq, comparator_34_eq,
       comparator_35_eq, comparator_36_eq, comparator_37_eq, comparator_38_eq, comparator_39_eq,
       comparator_40_eq, not_1_out, not_2_out, not_3_out, not_4_out, or_1_out, or_2_out, or_3_out, or_4_out,
       we_0, we_1, we_2, we_3;
  wire [1:0] Byte0_index, Byte1_index, Byte2_index, Byte3_index;
  wire [7:0] Byte0_data, Byte0_din, Byte0_out, Byte1_data, Byte1_din, Byte1_out, Byte2_data, Byte2_din,
       Byte2_out, Byte3_data, Byte3_din, Byte3_out, multiplexer_22_out, multiplexer_23_out,
       multiplexer_24_out, multiplexer_25_out, multiplexer_26_out, multiplexer_27_out, multiplexer_28_out,
       multiplexer_29_out, multiplexer_30_out, multiplexer_31_out, multiplexer_32_out, multiplexer_33_out;
  wire [15:0] adder_1_out, adder_2_out, adder_3_out, Byte0_addr, Byte0_block, Byte1_addr, Byte1_block,
       Byte2_addr, Byte2_block, Byte3_addr, Byte3_block, multiplexer_6_out, multiplexer_7_out,
       multiplexer_8_out, multiplexer_9_out, multiplexer_10_out, multiplexer_11_out, multiplexer_12_out,
       multiplexer_13_out, multiplexer_14_out, multiplexer_16_out, multiplexer_17_out, multiplexer_18_out;
  wire [31:0] bit_extender_2_out;

  RAM #(.addrWidth(16), .asyncread("true"), .clearpin("true")) ram_1 (
    .addr(Byte0_block), .we(we_0), .oe(1'b1), .clk(clk), .din(Byte0_din), .dout(Byte0_data), .clr(reset));
  RAM #(.addrWidth(16), .asyncread("true"), .clearpin("true")) ram_2 (
    .addr(Byte1_block), .we(we_1), .oe(1'b1), .clk(clk), .din(Byte1_din), .dout(Byte1_data), .clr(reset));
  RAM #(.addrWidth(16), .asyncread("true"), .clearpin("true")) ram_3 (
    .addr(Byte2_block), .we(we_2), .oe(1'b1), .clk(clk), .din(Byte2_din), .dout(Byte2_data), .clr(reset));
  RAM #(.addrWidth(16), .asyncread("true"), .clearpin("true")) ram_4 (
    .addr(Byte3_block), .we(we_3), .oe(1'b1), .clk(clk), .din(Byte3_din), .dout(Byte3_data), .clr(reset));
  Adder #(.width(16)) adder_1 (.a(mem_addr[15:0]), .b(16'h1), .out(adder_1_out));  // open: cin, cout
  Adder #(.width(16)) adder_2 (.a(mem_addr[15:0]), .b(16'h2), .out(adder_2_out));  // open: cin, cout
  Adder #(.width(16)) adder_3 (.a(mem_addr[15:0]), .b(16'h3), .out(adder_3_out));  // open: cin, cout
  Shifter #(.shift("lr"), .width(16)) shifter_1 (.in(mem_addr[15:0]), .\dist (4'b0010), .out(Byte0_addr));
  Shifter #(.shift("lr"), .width(16)) shifter_2 (.in(adder_1_out), .\dist (4'b0010), .out(Byte1_addr));
  Shifter #(.shift("lr"), .width(16)) shifter_3 (.in(adder_2_out), .\dist (4'b0010), .out(Byte2_addr));
  Shifter #(.shift("lr"), .width(16)) shifter_4 (.in(adder_3_out), .\dist (4'b0010), .out(Byte3_addr));
  Bit_Extender #(.in_width(16), .out_width(2), .\type ("zero")) bit_extender_1 (.in(mem_addr[15:0]), .out(Byte0_index));
  Adder #(.width(2)) adder_4 (.a(Byte0_index), .b(2'b01), .out(Byte1_index));  // open: cin, cout
  Adder #(.width(2)) adder_5 (.a(Byte1_index), .b(2'b01), .out(Byte2_index));  // open: cin, cout
  Adder #(.width(2)) adder_6 (.a(Byte2_index), .b(2'b01), .out(Byte3_index));  // open: cin, cout
  Multiplexer #(.select(2), .width(8)) multiplexer_1 (
    .in0(Byte0_data), .in1(Byte1_data), .in2(Byte2_data), .in3(Byte3_data), .out(Byte0_out), .sel(Byte0_index));
  Multiplexer #(.select(2), .width(8)) multiplexer_2 (
    .in0(Byte0_data), .in1(Byte1_data), .in2(Byte2_data), .in3(Byte3_data), .out(Byte1_out), .sel(Byte1_index));
  Multiplexer #(.select(2), .width(8)) multiplexer_3 (
    .in0(Byte0_data), .in1(Byte1_data), .in2(Byte2_data), .in3(Byte3_data), .out(Byte2_out), .sel(Byte2_index));
  Multiplexer #(.select(2), .width(8)) multiplexer_4 (
    .in0(Byte0_data), .in1(Byte1_data), .in2(Byte2_data), .in3(Byte3_data), .out(Byte3_out), .sel(Byte3_index));
  assign bit_extender_2_out = {{16{Byte1_out[7]}}, {Byte1_out, Byte0_out}};  // Bit_Extender bit_extender_2
  Multiplexer #(.width(32)) multiplexer_5 (
    .in0({Byte3_out, Byte2_out, Byte1_out, Byte0_out}), .in1(bit_extender_2_out), .out(mem_dout),
    .sel(if_half));
  Comparator #(.mode("unsigned"), .width(2)) comparator_1 (
    .a(Byte0_index), .b(2'b00), .eq(comparator_1_eq));  // open: gt, lt
  Comparator #(.mode("unsigned"), .width(2)) comparator_2 (
    .a(Byte1_index), .b(2'b00), .eq(comparator_2_eq));  // open: gt, lt
  Comparator #(.mode("unsigned"), .width(2)) comparator_3 (
    .a(Byte0_index), .b(2'b01), .eq(comparator_3_eq));  // open: gt, lt
  Comparator #(.mode("unsigned"), .width(2)) comparator_4 (
    .a(Byte1_index), .b(2'b01), .eq(comparator_4_eq));  // open: gt, lt
  Comparator #(.mode("unsigned"), .width(2)) comparator_5 (
    .a(Byte0_index), .b(2'b10), .eq(comparator_5_eq));  // open: gt, lt
  Comparator #(.mode("unsigned"), .width(2)) comparator_6 (
    .a(Byte1_index), .b(2'b10), .eq(comparator_6_eq));  // open: gt, lt
  Comparator #(.mode("unsigned"), .width(2)) comparator_7 (
    .a(Byte0_index), .b(2'b11), .eq(comparator_7_eq));  // open: gt, lt
  Comparator #(.mode("unsigned"), .width(2)) comparator_8 (
    .a(Byte1_index), .b(2'b11), .eq(comparator_8_eq));  // open: gt, lt
  or or_1 (or_1_out, comparator_1_eq, comparator_2_eq);
  or or_2 (or_2_out, comparator_3_eq, comparator_4_eq);
  or or_3 (or_3_out, comparator_5_eq, comparator_6_eq);
  or or_4 (or_4_out, comparator_7_eq, comparator_8_eq);
  and and_1 (and_1_out, or_1_out, if_half);
  not not_1 (not_1_out, if_half);
  and and_2 (and_2_out, or_2_out, if_half);
  not not_2 (not_2_out, if_half);
  and and_3 (and_3_out, or_3_out, if_half);
  not not_3 (not_3_out, if_half);
  and and_4 (and_4_out, or_4_out, if_half);
  not not_4 (not_4_out, if_half);
  or or_5 (we_0, and_1_out, not_1_out);
  or or_6 (we_1, and_2_out, not_2_out);
  or or_7 (we_2, and_3_out, not_3_out);
  or or_8 (we_3, and_4_out, not_4_out);
  Comparator #(.mode("unsigned"), .width(2)) comparator_9 (
    .a(Byte3_index), .b(2'b00), .eq(comparator_9_eq));  // open: gt, lt
  Multiplexer #(.width(16)) multiplexer_6 (
    .in0({16{1'b1}}), .in1(Byte3_addr), .out(multiplexer_6_out), .sel(comparator_9_eq));
  Comparator #(.mode("unsigned"), .width(2)) comparator_10 (
    .a(Byte3_index), .b(2'b01), .eq(comparator_10_eq));  // open: gt, lt
  Comparator #(.mode("unsigned"), .width(2)) comparator_11 (
    .a(Byte3_index), .b(2'b10), .eq(comparator_11_eq));  // open: gt, lt
  Comparator #(.mode("unsigned"), .width(2)) comparator_12 (
    .a(Byte3_index), .b(2'b11), .eq(comparator_12_eq));  // open: gt, lt
  Multiplexer #(.width(16)) multiplexer_7 (
    .in0(multiplexer_6_out), .in1(Byte2_addr), .out(multiplexer_7_out), .sel(comparator_13_eq));
  Comparator #(.mode("unsigned"), .width(2)) comparator_13 (
    .a(Byte2_index), .b(2'b00), .eq(comparator_13_eq));  // open: gt, lt
  Multiplexer #(.width(16)) multiplexer_8 (
    .in0({16{1'b1}}), .in1(Byte3_addr), .out(multiplexer_8_out), .sel(comparator_10_eq));
  Comparator #(.mode("unsigned"), .width(2)) comparator_14 (
    .a(Byte2_index), .b(2'b01), .eq(comparator_14_eq));  // open: gt, lt
  Multiplexer #(.width(16)) multiplexer_9 (
    .in0({16{1'b1}}), .in1(Byte3_addr), .out(multiplexer_9_out), .sel(comparator_11_eq));
  Comparator #(.mode("unsigned"), .width(2)) comparator_15 (
    .a(Byte2_index), .b(2'b10), .eq(comparator_15_eq));  // open: gt, lt
  Multiplexer #(.width(16)) multiplexer_10 (
    .in0({16{1'b1}}), .in1(Byte3_addr), .out(multiplexer_10_out), .sel(comparator_12_eq));
  Comparator #(.mode("unsigned"), .width(2)) comparator_16 (
    .a(Byte2_index), .b(2'b11), .eq(comparator_16_eq));  // open: gt, lt
  Multiplexer #(.width(16)) multiplexer_11 (
    .in0(multiplexer_7_out), .in1(Byte1_addr), .out(multiplexer_11_out), .sel(comparator_17_eq));
  Comparator #(.mode("unsigned"), .width(2)) comparator_17 (
    .a(Byte1_index), .b(2'b00), .eq(comparator_17_eq));  // open: gt, lt
  Multiplexer #(.width(16)) multiplexer_12 (
    .in0(multiplexer_8_out), .in1(Byte2_addr), .out(multiplexer_12_out), .sel(comparator_14_eq));
  Multiplexer #(.width(16)) multiplexer_13 (
    .in0(multiplexer_9_out), .in1(Byte2_addr), .out(multiplexer_13_out), .sel(comparator_15_eq));
  Multiplexer #(.width(16)) multiplexer_14 (
    .in0(multiplexer_10_out), .in1(Byte2_addr), .out(multiplexer_14_out), .sel(comparator_16_eq));
  Multiplexer #(.width(16)) multiplexer_15 (
    .in0(multiplexer_11_out), .in1(Byte0_addr), .out(Byte0_block), .sel(comparator_18_eq));
  Comparator #(.mode("unsigned"), .width(2)) comparator_18 (
    .a(Byte0_index), .b(2'b00), .eq(comparator_18_eq));  // open: gt, lt
  Multiplexer #(.width(16)) multiplexer_16 (
    .in0(multiplexer_12_out), .in1(Byte1_addr), .out(multiplexer_16_out), .sel(comparator_19_eq));
  Comparator #(.mode("unsigned"), .width(2)) comparator_19 (
    .a(Byte1_index), .b(2'b01), .eq(comparator_19_eq));  // open: gt, lt
  Multiplexer #(.width(16)) multiplexer_17 (
    .in0(multiplexer_13_out), .in1(Byte1_addr), .out(multiplexer_17_out), .sel(comparator_20_eq));
  Comparator #(.mode("unsigned"), .width(2)) comparator_20 (
    .a(Byte1_index), .b(2'b10), .eq(comparator_20_eq));  // open: gt, lt
  Multiplexer #(.width(16)) multiplexer_18 (
    .in0(multiplexer_14_out), .in1(Byte1_addr), .out(multiplexer_18_out), .sel(comparator_21_eq));
  Comparator #(.mode("unsigned"), .width(2)) comparator_21 (
    .a(Byte1_index), .b(2'b11), .eq(comparator_21_eq));  // open: gt, lt
  Multiplexer #(.width(16)) multiplexer_19 (
    .in0(multiplexer_16_out), .in1(Byte0_addr), .out(Byte1_block), .sel(comparator_22_eq));
  Comparator #(.mode("unsigned"), .width(2)) comparator_22 (
    .a(Byte0_index), .b(2'b01), .eq(comparator_22_eq));  // open: gt, lt
  Multiplexer #(.width(16)) multiplexer_20 (
    .in0(multiplexer_17_out), .in1(Byte0_addr), .out(Byte2_block), .sel(comparator_23_eq));
  Comparator #(.mode("unsigned"), .width(2)) comparator_23 (
    .a(Byte0_index), .b(2'b10), .eq(comparator_23_eq));  // open: gt, lt
  Multiplexer #(.width(16)) multiplexer_21 (
    .in0(multiplexer_18_out), .in1(Byte0_addr), .out(Byte3_block), .sel(comparator_24_eq));
  Comparator #(.mode("unsigned"), .width(2)) comparator_24 (
    .a(Byte0_index), .b(2'b11), .eq(comparator_24_eq));  // open: gt, lt
  Comparator #(.mode("unsigned"), .width(2)) comparator_25 (
    .a(Byte3_index), .b(2'b00), .eq(comparator_25_eq));  // open: gt, lt
  Comparator #(.mode("unsigned"), .width(2)) comparator_26 (
    .a(Byte3_index), .b(2'b01), .eq(comparator_26_eq));  // open: gt, lt
  Comparator #(.mode("unsigned"), .width(2)) comparator_27 (
    .a(Byte3_index), .b(2'b10), .eq(comparator_27_eq));  // open: gt, lt
  Comparator #(.mode("unsigned"), .width(2)) comparator_28 (
    .a(Byte3_index), .b(2'b11), .eq(comparator_28_eq));  // open: gt, lt
  Multiplexer #(.width(8)) multiplexer_22 (
    .in0({8{1'b1}}), .in1(mem_din[31:24]), .out(multiplexer_22_out), .sel(comparator_25_eq));
  Comparator #(.mode("unsigned"), .width(2)) comparator_29 (
    .a(Byte2_index), .b(2'b00), .eq(comparator_29_eq));  // open: gt, lt
  Multiplexer #(.width(8)) multiplexer_23 (
    .in0({8{1'b1}}), .in1(mem_din[31:24]), .out(multiplexer_23_out), .sel(comparator_26_eq));
  Comparator #(.mode("unsigned"), .width(2)) comparator_30 (
    .a(Byte2_index), .b(2'b01), .eq(comparator_30_eq));  // open: gt, lt
  Multiplexer #(.width(8)) multiplexer_24 (
    .in0({8{1'b1}}), .in1(mem_din[31:24]), .out(multiplexer_24_out), .sel(comparator_27_eq));
  Multiplexer #(.width(8)) multiplexer_25 (
    .in0({8{1'b1}}), .in1(mem_din[31:24]), .out(multiplexer_25_out), .sel(comparator_28_eq));
  Comparator #(.mode("unsigned"), .width(2)) comparator_31 (
    .a(Byte2_index), .b(2'b11), .eq(comparator_31_eq));  // open: gt, lt
  Multiplexer #(.width(8)) multiplexer_26 (
    .in0(multiplexer_22_out), .in1(mem_din[23:16]), .out(multiplexer_26_out), .sel(comparator_29_eq));
  Multiplexer #(.width(8)) multiplexer_27 (
    .in0(multiplexer_23_out), .in1(mem_din[23:16]), .out(multiplexer_27_out), .sel(comparator_30_eq));
  Multiplexer #(.width(8)) multiplexer_28 (
    .in0(multiplexer_24_out), .in1(mem_din[23:16]), .out(multiplexer_28_out), .sel(comparator_32_eq));
  Comparator #(.mode("unsigned"), .width(2)) comparator_32 (
    .a(Byte2_index), .b(2'b10), .eq(comparator_32_eq));  // open: gt, lt
  Multiplexer #(.width(8)) multiplexer_29 (
    .in0(multiplexer_25_out), .in1(mem_din[23:16]), .out(multiplexer_29_out), .sel(comparator_31_eq));
  Multiplexer #(.width(8)) multiplexer_30 (
    .in0(multiplexer_26_out), .in1(mem_din[15:8]), .out(multiplexer_30_out), .sel(comparator_33_eq));
  Comparator #(.mode("unsigned"), .width(2)) comparator_33 (
    .a(Byte1_index), .b(2'b00), .eq(comparator_33_eq));  // open: gt, lt
  Multiplexer #(.width(8)) multiplexer_31 (
    .in0(multiplexer_27_out), .in1(mem_din[15:8]), .out(multiplexer_31_out), .sel(comparator_34_eq));
  Comparator #(.mode("unsigned"), .width(2)) comparator_34 (
    .a(Byte1_index), .b(2'b01), .eq(comparator_34_eq));  // open: gt, lt
  Multiplexer #(.width(8)) multiplexer_32 (
    .in0(multiplexer_28_out), .in1(mem_din[15:8]), .out(multiplexer_32_out), .sel(comparator_35_eq));
  Comparator #(.mode("unsigned"), .width(2)) comparator_35 (
    .a(Byte1_index), .b(2'b10), .eq(comparator_35_eq));  // open: gt, lt
  Multiplexer #(.width(8)) multiplexer_33 (
    .in0(multiplexer_29_out), .in1(mem_din[15:8]), .out(multiplexer_33_out), .sel(comparator_36_eq));
  Comparator #(.mode("unsigned"), .width(2)) comparator_36 (
    .a(Byte1_index), .b(2'b11), .eq(comparator_36_eq));  // open: gt, lt
  Multiplexer #(.width(8)) multiplexer_34 (
    .in0(multiplexer_30_out), .in1(mem_din[7:0]), .out(Byte0_din), .sel(comparator_37_eq));
  Comparator #(.mode("unsigned"), .width(2)) comparator_37 (
    .a(Byte0_index), .b(2'b00), .eq(comparator_37_eq));  // open: gt, lt
  Multiplexer #(.width(8)) multiplexer_35 (
    .in0(multiplexer_31_out), .in1(mem_din[7:0]), .out(Byte1_din), .sel(comparator_38_eq));
  Comparator #(.mode("unsigned"), .width(2)) comparator_38 (
    .a(Byte0_index), .b(2'b01), .eq(comparator_38_eq));  // open: gt, lt
  Multiplexer #(.width(8)) multiplexer_36 (
    .in0(multiplexer_32_out), .in1(mem_din[7:0]), .out(Byte2_din), .sel(comparator_39_eq));
  Comparator #(.mode("unsigned"), .width(2)) comparator_39 (
    .a(Byte0_index), .b(2'b10), .eq(comparator_39_eq));  // open: gt, lt
  Multiplexer #(.width(8)) multiplexer_37 (
    .in0(multiplexer_33_out), .in1(mem_din[7:0]), .out(Byte3_din), .sel(comparator_40_eq));
  Comparator #(.mode("unsigned"), .width(2)) comparator_40 (
    .a(Byte0_index), .b(2'b11), .eq(comparator_40_eq));  // open: gt, lt

  // Other names for the same wires on the sheet: addr[15:0] = mem_addr[15:0]; data_0[7:0] = mem_din[7:0];
  //   data_1[7:0] = mem_din[15:8]; data_2[7:0] = mem_din[23:16]; data_3[7:0] = mem_din[31:24]; rst = reset;
  //   we = mem_wen
endmodule

module ID (
  input  [31:0] inst,
  output [4:0] rd,
  output [4:0] rs1,
  output [4:0] rs2
);

  wire R;

  Comparator #(.width(7)) comparator_1 (.a(7'b0110011), .b(inst[6:0]), .eq(R));  // open: gt, lt

  assign rd = inst[11:7];
  assign rs1 = inst[19:15];
  assign rs2 = inst[24:20];

  // Other names for the same wires on the sheet: opcode[6:0] = inst[6:0]; range14_12[2:0] = inst[14:12];
  //   range31_25[6:0] = inst[31:25]
endmodule

module regfile (
  input  reset,
  input  [4:0] rs1,
  input  [4:0] rs2,
  input  clk,
  input  [31:0] wb_data,
  input  wb_en,
  input  [4:0] wb_addr,
  output [31:0] rs1_data,
  output [31:0] rs2_data
);

  wire we_0, we_1, we_2, we_3, we_4, we_5, we_6, we_7, we_8, we_9, we_10, we_11, we_12, we_13, we_14, we_15,
       we_16, we_17, we_18, we_19, we_20, we_21, we_22, we_23, we_24, we_25, we_26, we_27, we_28, we_29,
       we_30, we_31;
  wire [31:0] x0_out, x1_out, x2_out, x3_out, x4_out, x5_out, x6_out, x7_out, x8_out, x9_out, x10_out,
       x11_out, x12_out, x13_out, x14_out, x15_out, x16_out, x17_out, x18_out, x19_out, x20_out, x21_out,
       x22_out, x23_out, x24_out, x25_out, x26_out, x27_out, x28_out, x29_out, x30_out, x31_out;

  Register #(.width(32)) register_1 (.D(wb_data), .en(we_0), .clk(clk), .Q(x0_out), .clr(reset));
  Register #(.width(32)) register_2 (.D(wb_data), .en(we_1), .clk(clk), .Q(x1_out), .clr(reset));
  Register #(.width(32)) register_3 (.D(wb_data), .en(we_2), .clk(clk), .Q(x2_out), .clr(reset));
  Register #(.width(32)) register_4 (.D(wb_data), .en(we_3), .clk(clk), .Q(x3_out), .clr(reset));
  Register #(.width(32)) register_5 (.D(wb_data), .en(we_4), .clk(clk), .Q(x4_out), .clr(reset));
  Register #(.width(32)) register_6 (.D(wb_data), .en(we_5), .clk(clk), .Q(x5_out), .clr(reset));
  Register #(.width(32)) register_7 (.D(wb_data), .en(we_6), .clk(clk), .Q(x6_out), .clr(reset));
  Register #(.width(32)) register_8 (.D(wb_data), .en(we_7), .clk(clk), .Q(x7_out), .clr(reset));
  Register #(.width(32)) register_9 (.D(wb_data), .en(we_8), .clk(clk), .Q(x8_out), .clr(reset));
  Register #(.width(32)) register_10 (.D(wb_data), .en(we_9), .clk(clk), .Q(x9_out), .clr(reset));
  Register #(.width(32)) register_11 (.D(wb_data), .en(we_10), .clk(clk), .Q(x10_out), .clr(reset));
  Register #(.width(32)) register_12 (.D(wb_data), .en(we_11), .clk(clk), .Q(x11_out), .clr(reset));
  Register #(.width(32)) register_13 (.D(wb_data), .en(we_12), .clk(clk), .Q(x12_out), .clr(reset));
  Register #(.width(32)) register_14 (.D(wb_data), .en(we_13), .clk(clk), .Q(x13_out), .clr(reset));
  Register #(.width(32)) register_15 (.D(wb_data), .en(we_14), .clk(clk), .Q(x14_out), .clr(reset));
  Register #(.width(32)) register_16 (.D(wb_data), .en(we_15), .clk(clk), .Q(x15_out), .clr(reset));
  Register #(.width(32)) register_17 (.D(wb_data), .en(we_16), .clk(clk), .Q(x16_out), .clr(reset));
  Register #(.width(32)) register_18 (.D(wb_data), .en(we_17), .clk(clk), .Q(x17_out), .clr(reset));
  Register #(.width(32)) register_19 (.D(wb_data), .en(we_18), .clk(clk), .Q(x18_out), .clr(reset));
  Register #(.width(32)) register_20 (.D(wb_data), .en(we_19), .clk(clk), .Q(x19_out), .clr(reset));
  Register #(.width(32)) register_21 (.D(wb_data), .en(we_20), .clk(clk), .Q(x20_out), .clr(reset));
  Register #(.width(32)) register_22 (.D(wb_data), .en(we_21), .clk(clk), .Q(x21_out), .clr(reset));
  Register #(.width(32)) register_23 (.D(wb_data), .en(we_22), .clk(clk), .Q(x22_out), .clr(reset));
  Register #(.width(32)) register_24 (.D(wb_data), .en(we_23), .clk(clk), .Q(x23_out), .clr(reset));
  Register #(.width(32)) register_25 (.D(wb_data), .en(we_24), .clk(clk), .Q(x24_out), .clr(reset));
  Register #(.width(32)) register_26 (.D(wb_data), .en(we_25), .clk(clk), .Q(x25_out), .clr(reset));
  Register #(.width(32)) register_27 (.D(wb_data), .en(we_26), .clk(clk), .Q(x26_out), .clr(reset));
  Register #(.width(32)) register_28 (.D(wb_data), .en(we_27), .clk(clk), .Q(x27_out), .clr(reset));
  Register #(.width(32)) register_29 (.D(wb_data), .en(we_28), .clk(clk), .Q(x28_out), .clr(reset));
  Register #(.width(32)) register_30 (.D(wb_data), .en(we_29), .clk(clk), .Q(x29_out), .clr(reset));
  Register #(.width(32)) register_31 (.D(wb_data), .en(we_30), .clk(clk), .Q(x30_out), .clr(reset));
  Register #(.width(32)) register_32 (.D(wb_data), .en(we_31), .clk(clk), .Q(x31_out), .clr(reset));
  Multiplexer #(.select(5), .width(32)) multiplexer_1 (
    .in0(x0_out), .in1(x1_out), .in2(x2_out), .in3(x3_out), .in4(x4_out), .in5(x5_out), .in6(x6_out),
    .in7(x7_out), .in8(x8_out), .in9(x9_out), .in10(x10_out), .in11(x11_out), .in12(x12_out), .in13(x13_out),
    .in14(x14_out), .in15(x15_out), .in16(x16_out), .in17(x17_out), .in18(x18_out), .in19(x19_out),
    .in20(x20_out), .in21(x21_out), .in22(x22_out), .in23(x23_out), .in24(x24_out), .in25(x25_out),
    .in26(x26_out), .in27(x27_out), .in28(x28_out), .in29(x29_out), .in30(x30_out), .in31(x31_out),
    .out(rs1_data), .sel(rs1));
  Multiplexer #(.select(5), .width(32)) multiplexer_2 (
    .in0(x0_out), .in1(x1_out), .in2(x2_out), .in3(x3_out), .in4(x4_out), .in5(x5_out), .in6(x6_out),
    .in7(x7_out), .in8(x8_out), .in9(x9_out), .in10(x10_out), .in11(x11_out), .in12(x12_out), .in13(x13_out),
    .in14(x14_out), .in15(x15_out), .in16(x16_out), .in17(x17_out), .in18(x18_out), .in19(x19_out),
    .in20(x20_out), .in21(x21_out), .in22(x22_out), .in23(x23_out), .in24(x24_out), .in25(x25_out),
    .in26(x26_out), .in27(x27_out), .in28(x28_out), .in29(x29_out), .in30(x30_out), .in31(x31_out),
    .out(rs2_data), .sel(rs2));
  Demultiplexer #(.select(5)) demultiplexer_1 (
    .out0(we_0), .out1(we_1), .out2(we_2), .out3(we_3), .out4(we_4), .out5(we_5), .out6(we_6), .out7(we_7),
    .out8(we_8), .out9(we_9), .out10(we_10), .out11(we_11), .out12(we_12), .out13(we_13), .out14(we_14),
    .out15(we_15), .out16(we_16), .out17(we_17), .out18(we_18), .out19(we_19), .out20(we_20), .out21(we_21),
    .out22(we_22), .out23(we_23), .out24(we_24), .out25(we_25), .out26(we_26), .out27(we_27), .out28(we_28),
    .out29(we_29), .out30(we_30), .out31(we_31), .in(wb_en), .sel(wb_addr));
endmodule

module ALU (
  input  [31:0] rs1,
  input  [31:0] rs2_or_imm,
  input  [2:0] ALU_control,
  output [31:0] result,
  output equal
);

  wire comparator_1_lt, comparator_2_lt;
  wire [4:0] bit_extender_1_out, bit_extender_2_out;
  wire [31:0] ADD_result, AND_result, RightShiftArith_result, RightShiftLogic_result, SetLessThan_result,
       SetLessThanUnsigned_result;

  Comparator #(.width(32)) comparator_1 (.a(rs1), .b(rs2_or_imm), .lt(comparator_1_lt));  // open: gt, eq
  Comparator #(.mode("unsigned"), .width(32)) comparator_2 (
    .a(rs1), .b(rs2_or_imm), .lt(comparator_2_lt));  // open: gt, eq
  Bit_Extender #(.in_width(32), .out_width(5)) bit_extender_1 (.in(rs2_or_imm), .out(bit_extender_1_out));
  Bit_Extender #(.in_width(32), .out_width(5)) bit_extender_2 (.in(rs2_or_imm), .out(bit_extender_2_out));
  Adder #(.width(32)) adder_1 (.a(rs1), .b(rs2_or_imm), .out(ADD_result));  // open: cin, cout
  assign AND_result = rs1 & rs2_or_imm;  // AND_Gate and_1, 32 bits wide
  Shifter #(.shift("lr"), .width(32)) shifter_1 (.in(rs1), .\dist (bit_extender_1_out), .out(RightShiftLogic_result));
  assign SetLessThan_result = {{31{1'b0}}, comparator_1_lt};  // Bit_Extender bit_extender_3
  Shifter #(.shift("ar"), .width(32)) shifter_2 (.in(rs1), .\dist (bit_extender_2_out), .out(RightShiftArith_result));
  assign SetLessThanUnsigned_result = {{31{1'b0}}, comparator_2_lt};  // Bit_Extender bit_extender_4
  Comparator #(.width(32)) comparator_3 (.a(rs1), .b(rs2_or_imm), .eq(equal));  // open: gt, lt
  Multiplexer #(.select(3), .width(32)) multiplexer_1 (
    .in0(ADD_result), .in1(AND_result), .in2(RightShiftLogic_result), .in3(SetLessThan_result),
    .in4(RightShiftArith_result), .in5(SetLessThanUnsigned_result), .out(result), .sel(ALU_control));  // open: in6, in7
endmodule

module Imm_gen (
  input  [31:0] inst,
  output [31:0] imm
);

  wire comparator_1_eq, comparator_2_eq, comparator_3_eq, comparator_6_eq, comparator_7_eq, imm_0, imm_11,
       is_B, is_I, is_S, is_U, is_UJ, multiplexer_3_out;
  wire [3:0] imm_4_1;
  wire [19:0] imm_31_12;
  wire [31:0] multiplexer_6_out;
  wire [31:21] immFor_UJ;

  Multiplexer #(.width(20)) multiplexer_1 (.in0({20{1'b0}}), .in1({20{1'b1}}), .out(imm_31_12), .sel(inst[31]));
  Multiplexer #(.width(4)) multiplexer_2 (.in0(inst[11:8]), .in1(inst[24:21]), .out(imm_4_1), .sel(is_I));
  Multiplexer multiplexer_3 (.in0(1'b0), .in1(inst[20]), .out(multiplexer_3_out), .sel(is_I));
  Multiplexer multiplexer_4 (.in0(inst[31]), .in1(inst[7]), .out(imm_11), .sel(is_B));
  Multiplexer multiplexer_5 (.in0(multiplexer_3_out), .in1(inst[7]), .out(imm_0), .sel(is_S));
  Comparator #(.width(5)) comparator_1 (.a(inst[6:2]), .b(5'b00100), .eq(comparator_1_eq));  // open: gt, lt
  Comparator #(.width(5)) comparator_2 (.a(inst[6:2]), .b({5{1'b0}}), .eq(comparator_2_eq));  // open: gt, lt
  Comparator #(.width(5)) comparator_3 (.a(inst[6:2]), .b(5'b11001), .eq(comparator_3_eq));  // open: gt, lt
  Comparator #(.width(5)) comparator_4 (.a(inst[6:2]), .b(5'b01000), .eq(is_S));  // open: gt, lt
  Comparator #(.width(5)) comparator_5 (.a(inst[6:2]), .b(5'b11000), .eq(is_B));  // open: gt, lt
  Comparator #(.width(5)) comparator_6 (.a(inst[6:2]), .b(5'b00101), .eq(comparator_6_eq));  // open: gt, lt
  Comparator #(.width(5)) comparator_7 (.a(inst[6:2]), .b(5'b01101), .eq(comparator_7_eq));  // open: gt, lt
  Comparator #(.width(5)) comparator_8 (.a(inst[6:2]), .b(5'b11011), .eq(is_UJ));  // open: gt, lt
  or or_1 (is_U, comparator_6_eq, comparator_7_eq);
  or or_2 (is_I, comparator_1_eq, comparator_2_eq, comparator_3_eq);
  Multiplexer #(.width(32)) multiplexer_6 (
    .in0({imm_31_12, imm_11, inst[30:25], imm_4_1, imm_0}), .in1({inst[31:12], {12{1'b0}}}),
    .out(multiplexer_6_out), .sel(is_U));
  Multiplexer #(.width(32)) multiplexer_7 (
    .in0(multiplexer_6_out), .in1({immFor_UJ, inst[31], inst[19:12], inst[20], inst[30:21], 1'b0}),
    .out(imm), .sel(is_UJ));
  Multiplexer #(.width(11)) multiplexer_8 (.in0({11{1'b0}}), .in1({11{1'b1}}), .out(immFor_UJ), .sel(inst[31]));

  // Other names for the same wires on the sheet: imm_t[31:0] = {imm_31_12, imm_11, inst[30:25], imm_4_1, imm_0};
  //   immFor_U[31:12] = inst[31:12]; immFor_UJ[20:1] = {inst[31], inst[19:12], inst[20], inst[30:21]};
  //   inst_31_12[19:0] = inst[31:12]; inst_20 = inst[20]; inst_24_21[3:0] = inst[24:21]; imm_10_5[5:0] = inst[30:25];
  //   inst_30_25[5:0] = inst[30:25]; inst_31 = inst[31]; opcode[4:0] = inst[6:2]; inst_7 = inst[7];
  //   inst_11_8[3:0] = inst[11:8]
endmodule

module controller (
  input  [31:0] inst,
  output is_beq,
  output if_rs2,
  output we,
  output [1:0] wb_src,
  output wb_en,
  output [2:0] ALU_control,
  output pc_src,
  output rs1_src,
  output jal_or_jalr,
  output if_half,
  output B_type
);

  wire and_2_out, and_3_out, and_4_out, and_5_out, and_6_out, and_7_out, and_8_out, comparator_1_eq,
       comparator_2_eq, comparator_3_eq, comparator_4_eq, comparator_5_eq, comparator_6_eq, comparator_8_eq,
       comparator_9_eq, comparator_10_eq, comparator_11_eq, comparator_12_eq, comparator_13_eq,
       comparator_14_eq, comparator_15_eq, comparator_16_eq, comparator_17_eq, comparator_18_eq,
       comparator_19_eq, comparator_20_eq, comparator_21_eq, comparator_22_eq, comparator_23_eq,
       comparator_24_eq, comparator_25_eq, comparator_26_eq, comparator_27_eq, comparator_28_eq,
       comparator_29_eq, comparator_30_eq, comparator_32_eq, comparator_35_eq, not_1_out, not_2_out,
       not_3_out, not_4_out, not_6_out, not_7_out, not_8_out, or_1_out, or_2_out, or_7_out;

  Comparator #(.mode("unsigned"), .width(7)) comparator_1 (
    .a(inst[6:0]), .b(7'b1100111), .eq(comparator_1_eq));  // open: gt, lt
  Comparator #(.mode("unsigned"), .width(7)) comparator_2 (
    .a(inst[6:0]), .b(7'b1101111), .eq(comparator_2_eq));  // open: gt, lt
  Comparator #(.mode("unsigned"), .width(3)) comparator_3 (
    .a(inst[14:12]), .b(3'b000), .eq(comparator_3_eq));  // open: gt, lt
  Comparator #(.mode("unsigned"), .width(7)) comparator_4 (
    .a(inst[6:0]), .b(7'b1100011), .eq(comparator_4_eq));  // open: gt, lt
  Comparator #(.mode("unsigned"), .width(7)) comparator_5 (
    .a(inst[6:0]), .b(7'b0110011), .eq(comparator_5_eq));  // open: gt, lt
  Comparator #(.mode("unsigned"), .width(7)) comparator_6 (
    .a(inst[6:0]), .b(7'b1100011), .eq(comparator_6_eq));  // open: gt, lt
  Comparator #(.mode("unsigned"), .width(7)) comparator_7 (.a(inst[6:0]), .b(7'b0100011), .eq(we));  // open: gt, lt
  Comparator #(.mode("unsigned"), .width(7)) comparator_8 (
    .a(inst[6:0]), .b(7'b0100011), .eq(comparator_8_eq));  // open: gt, lt
  Comparator #(.mode("unsigned"), .width(7)) comparator_9 (
    .a(inst[6:0]), .b(7'b1100011), .eq(comparator_9_eq));  // open: gt, lt
  Comparator #(.mode("unsigned"), .width(7)) comparator_10 (
    .a(inst[6:0]), .b(7'b1110011), .eq(comparator_10_eq));  // open: gt, lt
  Comparator #(.mode("unsigned"), .width(7)) comparator_11 (
    .a(inst[6:0]), .b(7'b0000011), .eq(comparator_11_eq));  // open: gt, lt
  Comparator #(.mode("unsigned"), .width(7)) comparator_12 (
    .a(inst[6:0]), .b(7'b0110111), .eq(comparator_12_eq));  // open: gt, lt
  Comparator #(.mode("unsigned"), .width(7)) comparator_13 (
    .a(inst[6:0]), .b(7'b1100111), .eq(comparator_13_eq));  // open: gt, lt
  Comparator #(.mode("unsigned"), .width(7)) comparator_14 (
    .a(inst[6:0]), .b(7'b1101111), .eq(comparator_14_eq));  // open: gt, lt
  Comparator #(.mode("unsigned"), .width(7)) comparator_15 (
    .a(inst[6:0]), .b(7'b0110011), .eq(comparator_15_eq));  // open: gt, lt
  Comparator #(.mode("unsigned"), .width(3)) comparator_16 (
    .a(inst[14:12]), .b(3'b010), .eq(comparator_16_eq));  // open: gt, lt
  Comparator #(.mode("unsigned"), .width(7)) comparator_17 (
    .a(inst[6:0]), .b(7'b0010011), .eq(comparator_17_eq));  // open: gt, lt
  Comparator #(.mode("unsigned"), .width(3)) comparator_18 (
    .a(inst[14:12]), .b(3'b011), .eq(comparator_18_eq));  // open: gt, lt
  Comparator #(.mode("unsigned"), .width(7)) comparator_19 (
    .a(inst[6:0]), .b(7'b0010011), .eq(comparator_19_eq));  // open: gt, lt
  Comparator #(.mode("unsigned"), .width(3)) comparator_20 (
    .a(inst[14:12]), .b(3'b111), .eq(comparator_20_eq));  // open: gt, lt
  Comparator #(.mode("unsigned"), .width(7)) comparator_21 (
    .a(inst[6:0]), .b(7'b0110011), .eq(comparator_21_eq));  // open: gt, lt
  Comparator #(.mode("unsigned"), .width(3)) comparator_22 (
    .a(inst[14:12]), .b(3'b010), .eq(comparator_22_eq));  // open: gt, lt
  Comparator #(.mode("unsigned"), .width(7)) comparator_23 (
    .a(inst[6:0]), .b(7'b0010011), .eq(comparator_23_eq));  // open: gt, lt
  Comparator #(.mode("unsigned"), .width(3)) comparator_24 (
    .a(inst[14:12]), .b(3'b101), .eq(comparator_24_eq));  // open: gt, lt
  Comparator #(.mode("unsigned"), .width(7)) comparator_25 (
    .a(inst[6:0]), .b(7'b0110011), .eq(comparator_25_eq));  // open: gt, lt
  Comparator #(.mode("unsigned"), .width(3)) comparator_26 (
    .a(inst[14:12]), .b(3'b101), .eq(comparator_26_eq));  // open: gt, lt
  Comparator #(.mode("unsigned"), .width(7)) comparator_27 (
    .a(inst[6:0]), .b(7'b0010011), .eq(comparator_27_eq));  // open: gt, lt
  Comparator #(.mode("unsigned"), .width(3)) comparator_28 (
    .a(inst[14:12]), .b(3'b011), .eq(comparator_28_eq));  // open: gt, lt
  and and_1 (is_beq, comparator_3_eq, comparator_4_eq);
  not not_1 (not_1_out, comparator_5_eq);
  not not_2 (not_2_out, comparator_6_eq);
  or or_1 (or_1_out, comparator_8_eq, comparator_9_eq);
  not not_3 (not_3_out, or_1_out);
  not not_4 (not_4_out, comparator_10_eq);
  or or_2 (or_2_out, comparator_11_eq, comparator_1_eq, comparator_2_eq);
  not not_5 (wb_src[0], or_2_out);
  or or_3 (wb_src[1], comparator_12_eq, comparator_13_eq, comparator_14_eq);
  and and_2 (and_2_out, comparator_15_eq, comparator_16_eq);
  and and_3 (and_3_out, comparator_17_eq, comparator_18_eq);
  and and_4 (and_4_out, comparator_19_eq, comparator_20_eq);
  and and_5 (and_5_out, comparator_21_eq, comparator_22_eq);
  and and_6 (and_6_out, comparator_23_eq, comparator_24_eq);
  and and_7 (and_7_out, comparator_25_eq, comparator_26_eq);
  and and_8 (and_8_out, comparator_27_eq, comparator_28_eq);
  and and_9 (if_rs2, not_1_out, not_2_out);
  not not_6 (not_6_out, comparator_29_eq);
  Comparator #(.mode("unsigned"), .width(7)) comparator_29 (
    .a(inst[6:0]), .b({7{1'b0}}), .eq(comparator_29_eq));  // open: gt, lt
  or or_4 (ALU_control[0], and_2_out, and_3_out, and_4_out);
  or or_5 (ALU_control[1], and_5_out, and_6_out);
  or or_6 (ALU_control[2], and_7_out, and_8_out);
  Comparator #(.mode("unsigned"), .width(7)) comparator_30 (
    .a(inst[6:0]), .b(7'b1110011), .eq(comparator_30_eq));  // open: gt, lt
  and and_10 (wb_en, not_3_out, not_4_out, not_6_out);
  Comparator #(.mode("unsigned"), .width(2)) comparator_31 (.a(2'b11), .b(inst[6:5]), .eq(B_type));  // open: gt, lt
  not not_7 (not_7_out, comparator_30_eq);
  not not_8 (not_8_out, is_beq);
  and and_11 (jal_or_jalr, B_type, not_7_out, not_8_out);
  Comparator #(.mode("unsigned"), .width(7)) comparator_32 (
    .a(inst[6:0]), .b(7'b1101111), .eq(comparator_32_eq));  // open: gt, lt
  Comparator #(.mode("unsigned"), .width(7)) comparator_33 (
    .a(inst[6:0]), .b(7'b1100111), .eq(pc_src));  // open: gt, lt
  Comparator #(.mode("unsigned"), .width(3)) comparator_34 (.a(inst[14:12]), .b(3'b001), .eq(if_half));  // open: gt, lt
  Comparator #(.mode("unsigned"), .width(7)) comparator_35 (
    .a(inst[6:0]), .b(7'b0010111), .eq(comparator_35_eq));  // open: gt, lt
  or or_7 (or_7_out, comparator_35_eq, comparator_32_eq);
  not not_9 (rs1_src, or_7_out);

  // Other names for the same wires on the sheet: ALU_1 = ALU_control[0]; ALU_2 = ALU_control[1];
  //   ALU_3 = ALU_control[2]; opcode[6:0] = inst[6:0]; funct3[2:0] = inst[14:12]; wb_src_1 = wb_src[0];
  //   wb_src_2 = wb_src[1]
endmodule
