// Logisim project proj_2_2_top.circ as structural Verilog: 8 circuits, main circuit TOP
module TOP (
  input  clk,
  input  rst,
  input  [31:0] inst,
  output [31:0] current_pc_if,
  output mem_wen_mem,
  output [31:0] mem_din_mem,
  output [31:0] mem_dout_mem,
  output [31:0] mem_addr_mem,
  output control_en_mem,
  output [31:0] control_pc_mem,
  output wb_en_wb,
  output [4:0] wb_addr_wb,
  output [31:0] wb_data_wb
);

  wire alu_1_equal, B_type, beq_jump, controller_1_b_type, controller_1_if_half, controller_1_if_rs2,
       controller_1_is_beq, controller_1_jal_or_jalr, controller_1_pc_src, controller_1_rs1_src,
       controller_1_wb_en, controller_1_we, equal_q, if_beq_q, if_half_q, jal_or_jalr, pc_src, register_8_q,
       register_9_q, register_10_q, register_12_q, register_14_q, register_16_q, register_17_q,
       register_18_q, rs1_src, wb_en_q;
  wire [1:0] controller_1_wb_src, register_11_q, register_27_q, wb_src_q;
  wire [2:0] controller_1_alu_control, register_13_q;
  wire [4:0] id_1_rd, id_1_rs1, id_1_rs2, rd_q, register_4_q;
  wire [31:0] adder_2_out, alu_1_result, imm_gen_1_imm, imm_q, inst_addr_q, multiplexer_1_out,
       multiplexer_2_out, multiplexer_3_out, multiplexer_4_out, multiplexer_5_out, not_1_out,
       pc_before_align, PCPlus4, regfile_1_rs1_data, regfile_1_rs2_data, register_1_q, register_2_q,
       register_3_q, register_5_q, register_6_q, register_7_q, register_19_q, register_20_q, register_22_q,
       register_24_q, register_25_q, register_26_q, register_29_q;

  Multiplexer #(.width(32)) multiplexer_1 (
    .in0(PCPlus4), .in1(control_pc_mem), .out(multiplexer_1_out), .sel(control_en_mem));
  Register #(.width(32)) PC (.D(multiplexer_1_out), .clk(clk), .Q(current_pc_if), .clr(rst));  // open: en
  Adder #(.width(32)) adder_1 (.a(32'h4), .b(current_pc_if), .out(PCPlus4));  // open: cin, cout
  Multiplexer #(.width(32)) multiplexer_2 (.in0(inst), .in1({32{1'b0}}), .out(multiplexer_2_out), .sel(rst));
  Register #(.width(32)) register_1 (.D(current_pc_if), .clk(clk), .Q(register_1_q), .clr(rst));  // open: en
  Register #(.width(32)) register_2 (.D(multiplexer_2_out), .clk(clk), .Q(register_2_q), .clr(rst));  // open: en
  Register #(.width(32)) register_3 (.D(PCPlus4), .clk(clk), .Q(register_3_q), .clr(rst));  // open: en
  ID id_1 (.inst(register_2_q), .rd(id_1_rd), .rs1(id_1_rs1), .rs2(id_1_rs2));
  Imm_gen imm_gen_1 (.inst(register_2_q), .imm(imm_gen_1_imm));
  controller controller_1 (
    .inst(register_2_q), .is_beq(controller_1_is_beq), .if_rs2(controller_1_if_rs2), .we(controller_1_we),
    .wb_src(controller_1_wb_src), .wb_en(controller_1_wb_en), .ALU_control(controller_1_alu_control),
    .pc_src(controller_1_pc_src), .rs1_src(controller_1_rs1_src), .jal_or_jalr(controller_1_jal_or_jalr),
    .if_half(controller_1_if_half), .B_type(controller_1_b_type));
  regfile regfile_1 (
    .reset(rst), .rs1(id_1_rs1), .rs2(id_1_rs2), .clk(clk), .wb_data(wb_data_wb), .wb_en(wb_en_wb),
    .wb_addr(wb_addr_wb), .rs1_data(regfile_1_rs1_data), .rs2_data(regfile_1_rs2_data));
  Register #(.width(32)) inst_addr (.D(register_1_q), .clk(clk), .Q(inst_addr_q), .clr(rst));  // open: en
  Register #(.width(5)) register_4 (.D(id_1_rd), .clk(clk), .Q(register_4_q), .clr(rst));  // open: en
  Register #(.width(32)) register_5 (.D(regfile_1_rs1_data), .clk(clk), .Q(register_5_q), .clr(rst));  // open: en
  Register #(.width(32)) register_6 (.D(regfile_1_rs2_data), .clk(clk), .Q(register_6_q), .clr(rst));  // open: en
  Register #(.width(32)) register_7 (.D(imm_gen_1_imm), .clk(clk), .Q(register_7_q), .clr(rst));  // open: en
  Register #(.width(1)) register_8 (.D(controller_1_is_beq), .clk(clk), .Q(register_8_q), .clr(rst));  // open: en
  Register #(.width(1)) register_9 (.D(controller_1_if_rs2), .clk(clk), .Q(register_9_q), .clr(rst));  // open: en
  Register #(.width(1)) register_10 (.D(controller_1_we), .clk(clk), .Q(register_10_q), .clr(rst));  // open: en
  Register #(.width(2)) register_11 (.D(controller_1_wb_src), .clk(clk), .Q(register_11_q), .clr(rst));  // open: en
  Register #(.width(1)) register_12 (.D(controller_1_wb_en), .clk(clk), .Q(register_12_q), .clr(rst));  // open: en
  Register #(.width(3)) register_13 (
    .D(controller_1_alu_control), .clk(clk), .Q(register_13_q), .clr(rst));  // open: en
  Register #(.width(1)) register_14 (.D(controller_1_pc_src), .clk(clk), .Q(register_14_q), .clr(rst));  // open: en
  Register #(.width(1)) register_15 (.D(controller_1_rs1_src), .clk(clk), .Q(rs1_src), .clr(rst));  // open: en
  Register #(.width(1)) register_16 (
    .D(controller_1_jal_or_jalr), .clk(clk), .Q(register_16_q), .clr(rst));  // open: en
  Register #(.width(1)) register_17 (.D(controller_1_if_half), .clk(clk), .Q(register_17_q), .clr(rst));  // open: en
  Register #(.width(1)) register_18 (.D(controller_1_b_type), .clk(clk), .Q(register_18_q), .clr(rst));  // open: en
  Register #(.width(32)) register_19 (.D(register_3_q), .clk(clk), .Q(register_19_q), .clr(rst));  // open: en
  Multiplexer #(.width(32)) multiplexer_3 (
    .in0(inst_addr_q), .in1(register_5_q), .out(multiplexer_3_out), .sel(rs1_src));
  Multiplexer #(.width(32)) multiplexer_4 (
    .in0(register_6_q), .in1(register_7_q), .out(multiplexer_4_out), .sel(register_9_q));
  ALU alu_1 (
    .rs1(multiplexer_3_out), .rs2_or_imm(multiplexer_4_out), .ALU_control(register_13_q),
    .result(alu_1_result), .equal(alu_1_equal));
  Register #(.width(32)) register_20 (.D(inst_addr_q), .clk(clk), .Q(register_20_q), .clr(rst));  // open: en
  Register #(.width(5)) rd (.D(register_4_q), .clk(clk), .Q(rd_q), .clr(rst));  // open: en
  Register #(.width(32)) imm (.D(register_7_q), .clk(clk), .Q(imm_q), .clr(rst));  // open: en
  Register #(.width(32)) ALU_result (.D(alu_1_result), .clk(clk), .Q(mem_addr_mem), .clr(rst));  // open: en
  Register #(.width(32)) rs2 (.D(register_6_q), .clk(clk), .Q(mem_din_mem), .clr(rst));  // open: en
  Register #(.width(1)) if_beq (.D(register_8_q), .clk(clk), .Q(if_beq_q), .clr(rst));  // open: en
  Register #(.width(1)) mem_we (.D(register_10_q), .clk(clk), .Q(mem_wen_mem), .clr(rst));  // open: en
  Register #(.width(2)) wb_src (.D(register_11_q), .clk(clk), .Q(wb_src_q), .clr(rst));  // open: en
  Register #(.width(1)) wb_en (.D(register_12_q), .clk(clk), .Q(wb_en_q), .clr(rst));  // open: en
  Register #(.width(1)) equal (.D(alu_1_equal), .clk(clk), .Q(equal_q), .clr(rst));  // open: en
  Register #(.width(1)) u_pc_src (.D(register_14_q), .clk(clk), .Q(pc_src), .clr(rst));  // open: en
  Register #(.width(1)) u_jal_or_jalr (.D(register_16_q), .clk(clk), .Q(jal_or_jalr), .clr(rst));  // open: en
  Register #(.width(1)) if_half (.D(register_17_q), .clk(clk), .Q(if_half_q), .clr(rst));  // open: en
  Register #(.width(1)) register_21 (.D(register_18_q), .clk(clk), .Q(B_type), .clr(rst));  // open: en
  Register #(.width(32)) register_22 (.D(register_19_q), .clk(clk), .Q(register_22_q), .clr(rst));  // open: en
  assign not_1_out = ~32'h1;  // NOT_Gate not_1, 32 bits wide
  assign control_pc_mem = not_1_out & pc_before_align;  // AND_Gate and_1, 32 bits wide
  Adder #(.width(32)) adder_2 (.a(register_20_q), .b(imm_q), .out(adder_2_out));  // open: cin, cout
  Multiplexer #(.width(32)) multiplexer_5 (
    .in0(adder_2_out), .in1(mem_addr_mem), .out(multiplexer_5_out), .sel(pc_src));
  or or_1 (control_en_mem, jal_or_jalr, beq_jump);
  mem mem_1 (
    .reset(rst), .mem_wen(mem_wen_mem), .mem_din(mem_din_mem), .mem_addr(mem_addr_mem), .clk(clk),
    .if_half(if_half_q), .mem_dout(mem_dout_mem));
  Multiplexer #(.width(32)) multiplexer_6 (
    .in0({32{1'b0}}), .in1(multiplexer_5_out), .out(pc_before_align), .sel(B_type));
  and and_2 (beq_jump, if_beq_q, equal_q);
  Register #(.width(5)) register_23 (.D(rd_q), .clk(clk), .Q(wb_addr_wb), .clr(rst));  // open: en
  Register #(.width(32)) register_24 (.D(imm_q), .clk(clk), .Q(register_24_q), .clr(rst));  // open: en
  Register #(.width(32)) register_25 (.D(mem_dout_mem), .clk(clk), .Q(register_25_q), .clr(rst));  // open: en
  Register #(.width(32)) register_26 (.D(mem_addr_mem), .clk(clk), .Q(register_26_q), .clr(rst));  // open: en
  Register #(.width(2)) register_27 (.D(wb_src_q), .clk(clk), .Q(register_27_q), .clr(rst));  // open: en
  Register #(.width(1)) register_28 (.D(wb_en_q), .clk(clk), .Q(wb_en_wb), .clr(rst));  // open: en
  Register #(.width(32)) register_29 (.D(register_22_q), .clk(clk), .Q(register_29_q), .clr(rst));  // open: en
  Multiplexer #(.select(2), .width(32)) multiplexer_7 (
    .in0(register_25_q), .in1(register_26_q), .in2(PCPlus4), .in3(register_24_q), .out(wb_data_wb),
    .sel(register_27_q));

  // Notes on the sheet:
  //   DON'T TOUCH!
  //   IF stage output
  //   MEM stage output
  //   WB stage output
endmodule

module testbench (
  input  rst,
  output [7:0] out_2,
  output [31:0] current_pc_if,
  output mem_wen_mem,
  output halt,
  output [31:0] mem_din_mem,
  output [31:0] mem_dout_mem,
  output [31:0] mem_addr_mem,
  output control_en_mem,
  output [31:0] control_pc_mem,
  output wb_en_wb,
  output [4:0] wb_addr_wb,
  output [31:0] wb_data_wb
);

  wire and_1_out, carry, clk, not_1_out, not_2_out, por_1_out, rst_t;
  wire [31:0] inst;

  not not_1 (not_1_out, inst[2]);
  not not_2 (not_2_out, inst[3]);
  POR por_1 (.out(por_1_out));
  Clock clock_1 (.out(clk));
  or or_1 (rst_t, rst, por_1_out);
  and and_1 (and_1_out, inst[0], inst[1], not_1_out, not_2_out, inst[4], inst[5], inst[6]);
  TOP top_1 (
    .clk(clk), .rst(rst_t), .inst(inst), .current_pc_if(current_pc_if), .mem_wen_mem(mem_wen_mem),
    .mem_din_mem(mem_din_mem), .mem_dout_mem(mem_dout_mem), .mem_addr_mem(mem_addr_mem),
    .control_en_mem(control_en_mem), .control_pc_mem(control_pc_mem), .wb_en_wb(wb_en_wb),
    .wb_addr_wb(wb_addr_wb), .wb_data_wb(wb_data_wb));
  or or_2 (halt, and_1_out, carry);
  Counter counter_1 (.clr(rst_t), .up(1'b1), .count(1'b1), .clk(clk), .carry(carry), .Q(out_2));  // open: load, D
  // ROM #(.line("quad"), .misaligned("true")) rom_1: pin names not known; wires that end beside it: current_pc_if[7:0], inst[7:0], inst[15:8], inst[23:16], inst[31:24]
  // Probe on inst

  // Notes on the sheet:
  //   DON'T TOUCH!
  //   contents of rom_1 (hex, n*v repeats v):
  //   93 0 30 0 97 14 0 0 37 15 0 0 33 1 10 0 93 d2 21 0 13 b3 40 0 93 d2 21 0 13 b3 40 0 93 f3 f1 0 23 24
  //   30 0 23 16 30 0 3 24 80 0 3 24 80 0 3 14 c0 0 97 14 c0 0 97 14 0 0 37 15
  //   IF stage output
  //   MEM stage output
  //   WB stage output
  //   test
endmodule

module mem (
  input  reset,
  input  mem_wen,
  input  [31:0] mem_din,
  input  [31:0] mem_addr,
  input  clk,
  input  if_half,
  output [31:0] mem_dout
);

  wire [3:0] line_enables;
  wire [31:0] bit_extender_1_out, ram_1_p13;

  Multiplexer #(.width(4)) multiplexer_1 (.in0(4'b1111), .in1(4'b0011), .out(line_enables), .sel(if_half));
  // RAM #(.addrWidth(16), .clearpin("true"), .enables("line"), .line("quad"), .misaligned("true")) ram_1: pin names not known; wires that end beside it: mem_addr[15:0], mem_wen, line_enables[0], line_enables[1], line_enables[2], line_enables[3], clk, mem_din[7:0], mem_din[15:8], mem_din[23:16], mem_din[31:24], reset, ram_1_p13[7:0], ram_1_p13[15:8], ram_1_p13[23:16], ram_1_p13[31:24]
  assign bit_extender_1_out = {{16{ram_1_p13[15]}}, ram_1_p13[15:0]};  // Bit_Extender bit_extender_1
  Multiplexer #(.width(32)) multiplexer_2 (.in0(ram_1_p13), .in1(bit_extender_1_out), .out(mem_dout), .sel(if_half));

  // Other names for the same wires on the sheet: addr[15:0] = mem_addr[15:0]; data_0[7:0] = mem_din[7:0];
  //   data_1[7:0] = mem_din[15:8]; data_2[7:0] = mem_din[23:16]; data_3[7:0] = mem_din[31:24]; rst = reset;
  //   we = mem_wen
endmodule

module ID (
  input  [31:0] inst,
  output [4:0] rd,
  output [4:0] rs1,
  output [4:0] rs2
);

  wire R;

  Comparator #(.width(7)) comparator_1 (.a(7'b0110011), .b(inst[6:0]), .eq(R));  // open: gt, lt

  assign rd = inst[11:7];
  assign rs1 = inst[19:15];
  assign rs2 = inst[24:20];

  // Other names for the same wires on the sheet: opcode[6:0] = inst[6:0]; range14_12[2:0] = inst[14:12];
  //   range31_25[6:0] = inst[31:25]
endmodule

module regfile (
  input  reset,
  input  [4:0] rs1,
  input  [4:0] rs2,
  input  clk,
  input  [31:0] wb_data,
  input  wb_en,
  input  [4:0] wb_addr,
  output [31:0] rs1_data,
  output [31:0] rs2_data
);

  wire we_0, we_1, we_2, we_3, we_4, we_5, we_6, we_7, we_8, we_9, we_10, we_11, we_12, we_13, we_14, we_15,
       we_16, we_17, we_18, we_19, we_20, we_21, we_22, we_23, we_24, we_25, we_26, we_27, we_28, we_29,
       we_30, we_31;
  wire [31:0] x0_out, x1_out, x2_out, x3_out, x4_out, x5_out, x6_out, x7_out, x8_out, x9_out, x10_out,
       x11_out, x12_out, x13_out, x14_out, x15_out, x16_out, x17_out, x18_out, x19_out, x20_out, x21_out,
       x22_out, x23_out, x24_out, x25_out, x26_out, x27_out, x28_out, x29_out, x30_out, x31_out;

  Register #(.trigger("falling"), .width(32)) register_1 (.D(wb_data), .en(we_0), .clk(clk), .Q(x0_out), .clr(reset));
  Register #(.trigger("falling"), .width(32)) register_2 (.D(wb_data), .en(we_1), .clk(clk), .Q(x1_out), .clr(reset));
  Register #(.trigger("falling"), .width(32)) register_3 (.D(wb_data), .en(we_2), .clk(clk), .Q(x2_out), .clr(reset));
  Register #(.trigger("falling"), .width(32)) register_4 (.D(wb_data), .en(we_3), .clk(clk), .Q(x3_out), .clr(reset));
  Register #(.trigger("falling"), .width(32)) register_5 (.D(wb_data), .en(we_4), .clk(clk), .Q(x4_out), .clr(reset));
  Register #(.trigger("falling"), .width(32)) register_6 (.D(wb_data), .en(we_5), .clk(clk), .Q(x5_out), .clr(reset));
  Register #(.trigger("falling"), .width(32)) register_7 (.D(wb_data), .en(we_6), .clk(clk), .Q(x6_out), .clr(reset));
  Register #(.trigger("falling"), .width(32)) register_8 (.D(wb_data), .en(we_7), .clk(clk), .Q(x7_out), .clr(reset));
  Register #(.trigger("falling"), .width(32)) register_9 (.D(wb_data), .en(we_8), .clk(clk), .Q(x8_out), .clr(reset));
  Register #(.trigger("falling"), .width(32)) register_10 (.D(wb_data), .en(we_9), .clk(clk), .Q(x9_out), .clr(reset));
  Register #(.trigger("falling"), .width(32)) register_11 (
    .D(wb_data), .en(we_10), .clk(clk), .Q(x10_out), .clr(reset));
  Register #(.trigger("falling"), .width(32)) register_12 (
    .D(wb_data), .en(we_11), .clk(clk), .Q(x11_out), .clr(reset));
  Register #(.trigger("falling"), .width(32)) register_13 (
    .D(wb_data), .en(we_12), .clk(clk), .Q(x12_out), .clr(reset));
  Register #(.trigger("falling"), .width(32)) register_14 (
    .D(wb_data), .en(we_13), .clk(clk), .Q(x13_out), .clr(reset));
  Register #(.trigger("falling"), .width(32)) register_15 (
    .D(wb_data), .en(we_14), .clk(clk), .Q(x14_out), .clr(reset));
  Register #(.trigger("falling"), .width(32)) register_16 (
    .D(wb_data), .en(we_15), .clk(clk), .Q(x15_out), .clr(reset));
  Register #(.trigger("falling"), .width(32)) register_17 (
    .D(wb_data), .en(we_16), .clk(clk), .Q(x16_out), .clr(reset));
  Register #(.trigger("falling"), .width(32)) register_18 (
    .D(wb_data), .en(we_17), .clk(clk), .Q(x17_out), .clr(reset));
  Register #(.trigger("falling"), .width(32)) register_19 (
    .D(wb_data), .en(we_18), .clk(clk), .Q(x18_out), .clr(reset));
  Register #(.trigger("falling"), .width(32)) register_20 (
    .D(wb_data), .en(we_19), .clk(clk), .Q(x19_out), .clr(reset));
  Register #(.trigger("falling"), .width(32)) register_21 (
    .D(wb_data), .en(we_20), .clk(clk), .Q(x20_out), .clr(reset));
  Register #(.trigger("falling"), .width(32)) register_22 (
    .D(wb_data), .en(we_21), .clk(clk), .Q(x21_out), .clr(reset));
  Register #(.trigger("falling"), .width(32)) register_23 (
    .D(wb_data), .en(we_22), .clk(clk), .Q(x22_out), .clr(reset));
  Register #(.trigger("falling"), .width(32)) register_24 (
    .D(wb_data), .en(we_23), .clk(clk), .Q(x23_out), .clr(reset));
  Register #(.trigger("falling"), .width(32)) register_25 (
    .D(wb_data), .en(we_24), .clk(clk), .Q(x24_out), .clr(reset));
  Register #(.trigger("falling"), .width(32)) register_26 (
    .D(wb_data), .en(we_25), .clk(clk), .Q(x25_out), .clr(reset));
  Register #(.trigger("falling"), .width(32)) register_27 (
    .D(wb_data), .en(we_26), .clk(clk), .Q(x26_out), .clr(reset));
  Register #(.trigger("falling"), .width(32)) register_28 (
    .D(wb_data), .en(we_27), .clk(clk), .Q(x27_out), .clr(reset));
  Register #(.trigger("falling"), .width(32)) register_29 (
    .D(wb_data), .en(we_28), .clk(clk), .Q(x28_out), .clr(reset));
  Register #(.trigger("falling"), .width(32)) register_30 (
    .D(wb_data), .en(we_29), .clk(clk), .Q(x29_out), .clr(reset));
  Register #(.trigger("falling"), .width(32)) register_31 (
    .D(wb_data), .en(we_30), .clk(clk), .Q(x30_out), .clr(reset));
  Register #(.trigger("falling"), .width(32)) register_32 (
    .D(wb_data), .en(we_31), .clk(clk), .Q(x31_out), .clr(reset));
  Multiplexer #(.select(5), .width(32)) multiplexer_1 (
    .in0(x0_out), .in1(x1_out), .in2(x2_out), .in3(x3_out), .in4(x4_out), .in5(x5_out), .in6(x6_out),
    .in7(x7_out), .in8(x8_out), .in9(x9_out), .in10(x10_out), .in11(x11_out), .in12(x12_out), .in13(x13_out),
    .in14(x14_out), .in15(x15_out), .in16(x16_out), .in17(x17_out), .in18(x18_out), .in19(x19_out),
    .in20(x20_out), .in21(x21_out), .in22(x22_out), .in23(x23_out), .in24(x24_out), .in25(x25_out),
    .in26(x26_out), .in27(x27_out), .in28(x28_out), .in29(x29_out), .in30(x30_out), .in31(x31_out),
    .out(rs1_data), .sel(rs1));
  Multiplexer #(.select(5), .width(32)) multiplexer_2 (
    .in0(x0_out), .in1(x1_out), .in2(x2_out), .in3(x3_out), .in4(x4_out), .in5(x5_out), .in6(x6_out),
    .in7(x7_out), .in8(x8_out), .in9(x9_out), .in10(x10_out), .in11(x11_out), .in12(x12_out), .in13(x13_out),
    .in14(x14_out), .in15(x15_out), .in16(x16_out), .in17(x17_out), .in18(x18_out), .in19(x19_out),
    .in20(x20_out), .in21(x21_out), .in22(x22_out), .in23(x23_out), .in24(x24_out), .in25(x25_out),
    .in26(x26_out), .in27(x27_out), .in28(x28_out), .in29(x29_out), .in30(x30_out), .in31(x31_out),
    .out(rs2_data), .sel(rs2));
  Demultiplexer #(.select(5)) demultiplexer_1 (
    .out0(we_0), .out1(we_1), .out2(we_2), .out3(we_3), .out4(we_4), .out5(we_5), .out6(we_6), .out7(we_7),
    .out8(we_8), .out9(we_9), .out10(we_10), .out11(we_11), .out12(we_12), .out13(we_13), .out14(we_14),
    .out15(we_15), .out16(we_16), .out17(we_17), .out18(we_18), .out19(we_19), .out20(we_20), .out21(we_21),
    .out22(we_22), .out23(we_23), .out24(we_24), .out25(we_25), .out26(we_26), .out27(we_27), .out28(we_28),
    .out29(we_29), .out30(we_30), .out31(we_31), .in(wb_en), .sel(wb_addr));
endmodule

module ALU (
  input  [31:0] rs1,
  input  [31:0] rs2_or_imm,
  input  [2:0] ALU_control,
  output [31:0] result,
  output equal
);

  wire comparator_1_lt, comparator_2_lt;
  wire [4:0] bit_extender_1_out, bit_extender_2_out;
  wire [31:0] ADD_result, AND_result, RightShiftArith_result, RightShiftLogic_result, SetLessThan_result,
       SetLessThanUnsigned_result;

  Comparator #(.width(32)) comparator_1 (.a(rs1), .b(rs2_or_imm), .lt(comparator_1_lt));  // open: gt, eq
  Comparator #(.mode("unsigned"), .width(32)) comparator_2 (
    .a(rs1), .b(rs2_or_imm), .lt(comparator_2_lt));  // open: gt, eq
  Bit_Extender #(.in_width(32), .out_width(5)) bit_extender_1 (.in(rs2_or_imm), .out(bit_extender_1_out));
  Bit_Extender #(.in_width(32), .out_width(5)) bit_extender_2 (.in(rs2_or_imm), .out(bit_extender_2_out));
  Adder #(.width(32)) adder_1 (.a(rs1), .b(rs2_or_imm), .out(ADD_result));  // open: cin, cout
  assign AND_result = rs1 & rs2_or_imm;  // AND_Gate and_1, 32 bits wide
  Shifter #(.shift("lr"), .width(32)) shifter_1 (.in(rs1), .\dist (bit_extender_1_out), .out(RightShiftLogic_result));
  assign SetLessThan_result = {{31{1'b0}}, comparator_1_lt};  // Bit_Extender bit_extender_3
  Shifter #(.shift("ar"), .width(32)) shifter_2 (.in(rs1), .\dist (bit_extender_2_out), .out(RightShiftArith_result));
  assign SetLessThanUnsigned_result = {{31{1'b0}}, comparator_2_lt};  // Bit_Extender bit_extender_4
  Comparator #(.width(32)) comparator_3 (.a(rs1), .b(rs2_or_imm), .eq(equal));  // open: gt, lt
  Multiplexer #(.select(3), .width(32)) multiplexer_1 (
    .in0(ADD_result), .in1(AND_result), .in2(RightShiftLogic_result), .in3(SetLessThan_result),
    .in4(RightShiftArith_result), .in5(SetLessThanUnsigned_result), .out(result), .sel(ALU_control));  // open: in6, in7
endmodule

module Imm_gen (
  input  [31:0] inst,
  output [31:0] imm
);

  wire comparator_1_eq, comparator_2_eq, comparator_3_eq, comparator_6_eq, comparator_7_eq, imm_0, imm_11,
       is_B, is_I, is_S, is_U, is_UJ, multiplexer_3_out;
  wire [3:0] imm_4_1;
  wire [19:0] imm_31_12;
  wire [31:0] multiplexer_6_out;
  wire [31:21] immFor_UJ;

  Multiplexer #(.width(20)) multiplexer_1 (.in0({20{1'b0}}), .in1({20{1'b1}}), .out(imm_31_12), .sel(inst[31]));
  Multiplexer #(.width(4)) multiplexer_2 (.in0(inst[11:8]), .in1(inst[24:21]), .out(imm_4_1), .sel(is_I));
  Multiplexer multiplexer_3 (.in0(1'b0), .in1(inst[20]), .out(multiplexer_3_out), .sel(is_I));
  Multiplexer multiplexer_4 (.in0(inst[31]), .in1(inst[7]), .out(imm_11), .sel(is_B));
  Multiplexer multiplexer_5 (.in0(multiplexer_3_out), .in1(inst[7]), .out(imm_0), .sel(is_S));
  Comparator #(.width(5)) comparator_1 (.a(inst[6:2]), .b(5'b00100), .eq(comparator_1_eq));  // open: gt, lt
  Comparator #(.width(5)) comparator_2 (.a(inst[6:2]), .b({5{1'b0}}), .eq(comparator_2_eq));  // open: gt, lt
  Comparator #(.width(5)) comparator_3 (.a(inst[6:2]), .b(5'b11001), .eq(comparator_3_eq));  // open: gt, lt
  Comparator #(.width(5)) comparator_4 (.a(inst[6:2]), .b(5'b01000), .eq(is_S));  // open: gt, lt
  Comparator #(.width(5)) comparator_5 (.a(inst[6:2]), .b(5'b11000), .eq(is_B));  // open: gt, lt
  Comparator #(.width(5)) comparator_6 (.a(inst[6:2]), .b(5'b00101), .eq(comparator_6_eq));  // open: gt, lt
  Comparator #(.width(5)) comparator_7 (.a(inst[6:2]), .b(5'b01101), .eq(comparator_7_eq));  // open: gt, lt
  Comparator #(.width(5)) comparator_8 (.a(inst[6:2]), .b(5'b11011), .eq(is_UJ));  // open: gt, lt
  or or_1 (is_U, comparator_6_eq, comparator_7_eq);
  or or_2 (is_I, comparator_1_eq, comparator_2_eq, comparator_3_eq);
  Multiplexer #(.width(32)) multiplexer_6 (
    .in0({imm_31_12, imm_11, inst[30:25], imm_4_1, imm_0}), .in1({inst[31:12], {12{1'b0}}}),
    .out(multiplexer_6_out), .sel(is_U));
  Multiplexer #(.width(32)) multiplexer_7 (
    .in0(multiplexer_6_out), .in1({immFor_UJ, inst[31], inst[19:12], inst[20], inst[30:21], 1'b0}),
    .out(imm), .sel(is_UJ));
  Multiplexer #(.width(11)) multiplexer_8 (.in0({11{1'b0}}), .in1({11{1'b1}}), .out(immFor_UJ), .sel(inst[31]));

  // Other names for the same wires on the sheet: imm_t[31:0] = {imm_31_12, imm_11, inst[30:25], imm_4_1, imm_0};
  //   immFor_U[31:12] = inst[31:12]; immFor_UJ[20:1] = {inst[31], inst[19:12], inst[20], inst[30:21]};
  //   inst_31_12[19:0] = inst[31:12]; inst_20 = inst[20]; inst_24_21[3:0] = inst[24:21]; imm_10_5[5:0] = inst[30:25];
  //   inst_30_25[5:0] = inst[30:25]; inst_31 = inst[31]; opcode[4:0] = inst[6:2]; inst_7 = inst[7];
  //   inst_11_8[3:0] = inst[11:8]
endmodule

module controller (
  input  [31:0] inst,
  output is_beq,
  output if_rs2,
  output we,
  output [1:0] wb_src,
  output wb_en,
  output [2:0] ALU_control,
  output pc_src,
  output rs1_src,
  output jal_or_jalr,
  output if_half,
  output B_type
);

  wire and_2_out, and_3_out, and_4_out, and_5_out, and_6_out, and_7_out, and_8_out, comparator_1_eq,
       comparator_2_eq, comparator_3_eq, comparator_4_eq, comparator_5_eq, comparator_6_eq, comparator_8_eq,
       comparator_9_eq, comparator_10_eq, comparator_11_eq, comparator_12_eq, comparator_13_eq,
       comparator_14_eq, comparator_15_eq, comparator_16_eq, comparator_17_eq, comparator_18_eq,
       comparator_19_eq, comparator_20_eq, comparator_21_eq, comparator_22_eq, comparator_23_eq,
       comparator_24_eq, comparator_25_eq, comparator_26_eq, comparator_27_eq, comparator_28_eq,
       comparator_29_eq, comparator_30_eq, comparator_32_eq, comparator_35_eq, not_1_out, not_2_out,
       not_3_out, not_4_out, not_6_out, not_7_out, not_8_out, or_1_out, or_2_out, or_7_out;

  Comparator #(.mode("unsigned"), .width(7)) comparator_1 (
    .a(inst[6:0]), .b(7'b1100111), .eq(comparator_1_eq));  // open: gt, lt
  Comparator #(.mode("unsigned"), .width(7)) comparator_2 (
    .a(inst[6:0]), .b(7'b1101111), .eq(comparator_2_eq));  // open: gt, lt
  Comparator #(.mode("unsigned"), .width(3)) comparator_3 (
    .a(inst[14:12]), .b(3'b000), .eq(comparator_3_eq));  // open: gt, lt
  Comparator #(.mode("unsigned"), .width(7)) comparator_4 (
    .a(inst[6:0]), .b(7'b1100011), .eq(comparator_4_eq));  // open: gt, lt
  Comparator #(.mode("unsigned"), .width(7)) comparator_5 (
    .a(inst[6:0]), .b(7'b0110011), .eq(comparator_5_eq));  // open: gt, lt
  Comparator #(.mode("unsigned"), .width(7)) comparator_6 (
    .a(inst[6:0]), .b(7'b1100011), .eq(comparator_6_eq));  // open: gt, lt
  Comparator #(.mode("unsigned"), .width(7)) comparator_7 (.a(inst[6:0]), .b(7'b0100011), .eq(we));  // open: gt, lt
  Comparator #(.mode("unsigned"), .width(7)) comparator_8 (
    .a(inst[6:0]), .b(7'b0100011), .eq(comparator_8_eq));  // open: gt, lt
  Comparator #(.mode("unsigned"), .width(7)) comparator_9 (
    .a(inst[6:0]), .b(7'b1100011), .eq(comparator_9_eq));  // open: gt, lt
  Comparator #(.mode("unsigned"), .width(7)) comparator_10 (
    .a(inst[6:0]), .b(7'b1110011), .eq(comparator_10_eq));  // open: gt, lt
  Comparator #(.mode("unsigned"), .width(7)) comparator_11 (
    .a(inst[6:0]), .b(7'b0000011), .eq(comparator_11_eq));  // open: gt, lt
  Comparator #(.mode("unsigned"), .width(7)) comparator_12 (
    .a(inst[6:0]), .b(7'b0110111), .eq(comparator_12_eq));  // open: gt, lt
  Comparator #(.mode("unsigned"), .width(7)) comparator_13 (
    .a(inst[6:0]), .b(7'b1100111), .eq(comparator_13_eq));  // open: gt, lt
  Comparator #(.mode("unsigned"), .width(7)) comparator_14 (
    .a(inst[6:0]), .b(7'b1101111), .eq(comparator_14_eq));  // open: gt, lt
  Comparator #(.mode("unsigned"), .width(7)) comparator_15 (
    .a(inst[6:0]), .b(7'b0110011), .eq(comparator_15_eq));  // open: gt, lt
  Comparator #(.mode("unsigned"), .width(3)) comparator_16 (
    .a(inst[14:12]), .b(3'b010), .eq(comparator_16_eq));  // open: gt, lt
  Comparator #(.mode("unsigned"), .width(7)) comparator_17 (
    .a(inst[6:0]), .b(7'b0010011), .eq(comparator_17_eq));  // open: gt, lt
  Comparator #(.mode("unsigned"), .width(3)) comparator_18 (
    .a(inst[14:12]), .b(3'b011), .eq(comparator_18_eq));  // open: gt, lt
  Comparator #(.mode("unsigned"), .width(7)) comparator_19 (
    .a(inst[6:0]), .b(7'b0010011), .eq(comparator_19_eq));  // open: gt, lt
  Comparator #(.mode("unsigned"), .width(3)) comparator_20 (
    .a(inst[14:12]), .b(3'b111), .eq(comparator_20_eq));  // open: gt, lt
  Comparator #(.mode("unsigned"), .width(7)) comparator_21 (
    .a(inst[6:0]), .b(7'b0110011), .eq(comparator_21_eq));  // open: gt, lt
  Comparator #(.mode("unsigned"), .width(3)) comparator_22 (
    .a(inst[14:12]), .b(3'b010), .eq(comparator_22_eq));  // open: gt, lt
  Comparator #(.mode("unsigned"), .width(7)) comparator_23 (
    .a(inst[6:0]), .b(7'b0010011), .eq(comparator_23_eq));  // open: gt, lt
  Comparator #(.mode("unsigned"), .width(3)) comparator_24 (
    .a(inst[14:12]), .b(3'b101), .eq(comparator_24_eq));  // open: gt, lt
  Comparator #(.mode("unsigned"), .width(7)) comparator_25 (
    .a(inst[6:0]), .b(7'b0110011), .eq(comparator_25_eq));  // open: gt, lt
  Comparator #(.mode("unsigned"), .width(3)) comparator_26 (
    .a(inst[14:12]), .b(3'b101), .eq(comparator_26_eq));  // open: gt, lt
  Comparator #(.mode("unsigned"), .width(7)) comparator_27 (
    .a(inst[6:0]), .b(7'b0010011), .eq(comparator_27_eq));  // open: gt, lt
  Comparator #(.mode("unsigned"), .width(3)) comparator_28 (
    .a(inst[14:12]), .b(3'b011), .eq(comparator_28_eq));  // open: gt, lt
  and and_1 (is_beq, comparator_3_eq, comparator_4_eq);
  not not_1 (not_1_out, comparator_5_eq);
  not not_2 (not_2_out, comparator_6_eq);
  or or_1 (or_1_out, comparator_8_eq, comparator_9_eq);
  not not_3 (not_3_out, or_1_out);
  not not_4 (not_4_out, comparator_10_eq);
  or or_2 (or_2_out, comparator_11_eq, comparator_1_eq, comparator_2_eq);
  not not_5 (wb_src[0], or_2_out);
  or or_3 (wb_src[1], comparator_12_eq, comparator_13_eq, comparator_14_eq);
  and and_2 (and_2_out, comparator_15_eq, comparator_16_eq);
  and and_3 (and_3_out, comparator_17_eq, comparator_18_eq);
  and and_4 (and_4_out, comparator_19_eq, comparator_20_eq);
  and and_5 (and_5_out, comparator_21_eq, comparator_22_eq);
  and and_6 (and_6_out, comparator_23_eq, comparator_24_eq);
  and and_7 (and_7_out, comparator_25_eq, comparator_26_eq);
  and and_8 (and_8_out, comparator_27_eq, comparator_28_eq);
  and and_9 (if_rs2, not_1_out, not_2_out);
  not not_6 (not_6_out, comparator_29_eq);
  Comparator #(.mode("unsigned"), .width(7)) comparator_29 (
    .a(inst[6:0]), .b({7{1'b0}}), .eq(comparator_29_eq));  // open: gt, lt
  or or_4 (ALU_control[0], and_2_out, and_3_out, and_4_out);
  or or_5 (ALU_control[1], and_5_out, and_6_out);
  or or_6 (ALU_control[2], and_7_out, and_8_out);
  Comparator #(.mode("unsigned"), .width(7)) comparator_30 (
    .a(inst[6:0]), .b(7'b1110011), .eq(comparator_30_eq));  // open: gt, lt
  and and_10 (wb_en, not_3_out, not_4_out, not_6_out);
  Comparator #(.mode("unsigned"), .width(2)) comparator_31 (.a(2'b11), .b(inst[6:5]), .eq(B_type));  // open: gt, lt
  not not_7 (not_7_out, comparator_30_eq);
  not not_8 (not_8_out, is_beq);
  and and_11 (jal_or_jalr, B_type, not_7_out, not_8_out);
  Comparator #(.mode("unsigned"), .width(7)) comparator_32 (
    .a(inst[6:0]), .b(7'b1101111), .eq(comparator_32_eq));  // open: gt, lt
  Comparator #(.mode("unsigned"), .width(7)) comparator_33 (
    .a(inst[6:0]), .b(7'b1100111), .eq(pc_src));  // open: gt, lt
  Comparator #(.mode("unsigned"), .width(3)) comparator_34 (.a(inst[14:12]), .b(3'b001), .eq(if_half));  // open: gt, lt
  Comparator #(.mode("unsigned"), .width(7)) comparator_35 (
    .a(inst[6:0]), .b(7'b0010111), .eq(comparator_35_eq));  // open: gt, lt
  or or_7 (or_7_out, comparator_35_eq, comparator_32_eq);
  not not_9 (rs1_src, or_7_out);

  // Other names for the same wires on the sheet: ALU_1 = ALU_control[0]; ALU_2 = ALU_control[1];
  //   ALU_3 = ALU_control[2]; opcode[6:0] = inst[6:0]; funct3[2:0] = inst[14:12]; wb_src_1 = wb_src[0];
  //   wb_src_2 = wb_src[1]
endmodule
